# Fritzing sketch Fritzing_Sketch_Steckplatine (saved by Fritzing 0.9.6b)
breadboards: 1

parts:
  Mod1 = Raspberry Pi 4B
  DHT1 = DHT22 Humidity and Temperature Sensor
  DHT2 = DHT22 Humidity and Temperature Sensor
  R1 = Resistor [tolerance=±5% power=0.25 resistance=220 package=THT]
  R2 = Resistor [tolerance=±5% power=0.25 resistance=220 package=THT]
  U1 = Module 4 Relais 5V [package="Module 4 Relais 5V"]
  LED1 = LED - 5mm [color="Yellow (595nm)" current=0.030 package="5 mm [THT]"]
  R3 = Resistor [tolerance=±5% power=0.25 resistance=220 package=THT]

nets:
  N1: Mod1.5V, U1.JD-VCC
  GND: Mod1.GND, DHT1.GND, DHT2.GND, U1.GND, LED1.cathode
  N2: Mod1.GPIO27, DHT2.DATA, R2.Pin_1
  N3: Mod1.GPIO22, DHT1.DATA, R1.Pin_0
  N4: Mod1.GPIO10, U1.IN1
  VDD: Mod1.GPIO9, DHT1.VDD, DHT2.VDD, R1.Pin_1, R2.Pin_0, U1.VCC
  N5: Mod1.GPIO11, R3.Pin_1
  N6: LED1.anode, R3.Pin_0

notes:
  3.3V
  5.0V
  +
  -

custom parts:
  Module 4 Relais 5V: Module 4 Relais 5V 4x SPD-06VDC-SD-C
